# Fritzing sketch PID_Rough_Draft (saved by Fritzing 0.9.3b)
breadboards: 4

parts:
  Part1 = Arduino Uno (Rev3)
  Q1 = PHOTOTRANSISTOR REFLECTIVE OBJECT SENSOR [package=qrb1114-side]
  Q2 = NPN-Transistor [package="SOT-23 [SMD]"]
  R2 = Resistor [tolerance=±5% resistance=220 package=THT]
  M2 = DC Motor
  D2 = Diode [package=diode-1n4148]
  U2 = POT [package=3362u]  # not connected
  R3 = Rotary Potentiometer (Small) [maximum_resistance=100kΩ package=THT]
  Part2 = Arduino Uno (Rev3)
  VCC4 = Battery
  VCC3 = Battery
  VCC5 = Battery
  S1 = Toggle Switch [package=THT]  # not connected
  LED1 = LED - 5mm [color="Red (633nm)" package="5 mm [THT]"]  # not connected

nets:
  N1: Part1.A5/SCL, R3.wiper
  N2: Part1.D11_PWM/MOSI, R2.Pin_0
  N3: Part1.D2, Part1.D3_PWM, Q1.C
  N4: Part1.5V, Q1.A, Q1.K, R3.leg2
  N5: Part1.GND, Q1.E, Q2.1, R3.leg1
  N6: Q2.0, R2.Pin_1
  N7: M2.pin_1, D2.C
  N8: Part2.GND, VCC5.-
  N9: VCC4.-, VCC3.+
